// Logisim project hw4.circ as structural Verilog: 1 circuit, main circuit Attempt 2
module Attempt_2 (
  input  A,
  input  B,
  input  C,
  input  D
);

  wire A_Not_B_C, B_D_Not_A, B_D_Not_A_C, B_Not_A, B_Not_A_C, B_Not_A_D, C_D_Not_A, C_Not_A, C_Not_A_B,
       C_Not_A_D, D_Not_A, Not_A, Not_A_B, Not_A_C_D, Not_B, Not_B_C, Not_B_C_D, Not_C, Not_D, or_1_out,
       or_2_out, or_3_out, or_4_out, or_5_out, or_6_out, or_7_out;

  not not_1 (Not_A, A);
  not not_2 (Not_B, B);
  not not_3 (Not_C, C);
  not not_4 (Not_D, D);
  and and_1 (B_D_Not_A_C, Not_A, B, Not_C, D);
  and and_2 (A_Not_B_C, A, Not_B, Not_C);
  and and_3 (B_D_Not_A, Not_A, B, D);
  and and_4 (C_Not_A, Not_A, C);
  and and_5 (Not_B_C, Not_B, Not_C);
  and and_6 (Not_A_B, Not_A, Not_B);
  and and_7 (Not_A_C_D, Not_A, Not_C, Not_D);
  and and_8 (C_D_Not_A, Not_A, C, D);
  and and_9 (Not_B_C_D, Not_B, Not_C, Not_D);
  and and_10 (B_Not_A_C, Not_A, B, Not_C);
  and and_11 (B_Not_A_D, Not_A, B, Not_D);
  or or_1 (or_1_out, Not_B_C_D, A_Not_B_C, B_D_Not_A, C_Not_A);
  or or_2 (or_2_out, Not_B_C, Not_A_B, Not_A_C_D, C_D_Not_A);
  or or_3 (or_3_out, Not_B_C_D, B_Not_A_C, B_Not_A_D, A_Not_B_C);
  or or_4 (or_4_out, C_Not_A_B, B_Not_A_C, B_Not_A_D, A_Not_B_C);
  _7_Segment_Display u_7_segment_display_1 (
    .g(or_4_out), .f(or_3_out), .a(or_1_out), .b(or_2_out), .e(or_6_out), .d(or_7_out), .c(or_5_out));  // open: dp
  and and_12 (C_Not_A_B, Not_A, Not_B, C);
  or or_5 (or_5_out, Not_B_C, D_Not_A, B_Not_A);
  or or_6 (or_6_out, Not_B_C_D, C_Not_A_D);
  or or_7 (or_7_out, Not_B_C_D, C_Not_A_B, C_Not_A_D, A_Not_B_C, B_D_Not_A_C);
  and and_13 (D_Not_A, D, Not_A);
  and and_14 (B_Not_A, Not_A, B);
  and and_15 (C_Not_A_D, Not_A, C, Not_D);

  // Notes on the sheet:
  //   m7
  //   m1
  //   m2
  //   m4
  //   m1
  //   m2
  //   m3
  //   m3
  //   m4
  //   m5
  //   m5
  //   m6
  //   m7
  //   m6
endmodule
